// Logisim project jump.circ as structural Verilog: 1 circuit, main circuit main
module main (
);

  wire and_1_out, bitselector_1_out, bitselector_2_out, bitselector_3_out, multiplexer_1_out, or_1_out,
       undriven, undriven_2, undriven_3, undriven_4;

  LED led_1 (.in(undriven));
  LED led_2 ();  // open: in
  LED led_3 (.in(undriven_3));
  LED led_4 (.in(undriven_4));
  LED led_5 ();  // open: in
  LED led_6 ();  // open: in
  LED led_7 (.in(undriven_2));
  BitSelector #(.width(1)) bitselector_1 (.in(undriven_2), .out(bitselector_1_out));  // open: sel
  BitSelector #(.width(1)) bitselector_2 (.in(undriven_2), .out(bitselector_2_out));  // open: sel
  or or_1 (or_1_out, bitselector_2_out, bitselector_3_out);
  BitSelector #(.width(1)) bitselector_3 (.in(undriven_2), .out(bitselector_3_out));  // open: sel
  and and_1 (and_1_out, bitselector_1_out, or_1_out);
  LED led_8 (.in(undriven));
  Multiplexer multiplexer_1 (.in0(undriven_3), .in1(undriven_4), .out(multiplexer_1_out), .sel(and_1_out));
  LED led_9 (.in(multiplexer_1_out));

  // Notes on the sheet:
  //   rd_addr
  //   flags
  //   imm
  //   flag_mask1
  //   flag_mask2
  //   opcode
  //   pc_old
  //   0
  //   1
  //   3
  //   flags_ok
endmodule
